// Logisim project d8421_5.circ as structural Verilog: 1 circuit, main circuit main
module main (
  input  [3:0] in_1,
  output [3:0] out_2,
  output [3:0] out_3,
  output [3:0] out_4
);

  wire not_1_out, not_2_out, not_3_out, not_4_out, or_1_out, or_2_out, or_3_out, or_4_out, or_5_out,
       or_6_out, or_7_out, or_8_out, or_9_out, or_10_out, or_11_out, or_12_out, or_13_out;

  not not_1 (not_1_out, in_1[1]);
  not not_2 (not_2_out, in_1[3]);
  not not_3 (not_3_out, in_1[0]);
  not not_4 (not_4_out, in_1[2]);
  or or_1 (or_1_out, in_1[2], in_1[1]);
  or or_2 (or_2_out, in_1[3], not_1_out, in_1[0]);
  or or_3 (or_3_out, in_1[3], not_4_out, not_3_out);
  or or_4 (or_4_out, not_2_out, in_1[2], in_1[1], in_1[0]);
  or or_5 (or_5_out, in_1[3], not_4_out);
  or or_6 (or_6_out, in_1[3], not_1_out, not_3_out);
  or or_7 (or_7_out, in_1[3], in_1[2], not_1_out, not_3_out);
  or or_8 (or_8_out, not_2_out, in_1[2], in_1[1], not_3_out);
  or or_9 (or_9_out, in_1[3], in_1[1], in_1[0]);
  or or_10 (or_10_out, in_1[3], not_4_out, in_1[1]);
  or or_11 (or_11_out, in_1[3], not_4_out, in_1[0]);
  or or_12 (or_12_out, in_1[2], in_1[1], not_3_out);
  or or_13 (or_13_out, in_1[3], not_3_out);
  and and_1 (out_3[3], or_1_out, or_2_out, or_3_out);
  and and_2 (out_3[2], or_4_out, or_5_out, or_6_out);
  and and_3 (out_3[1], or_7_out, or_8_out, or_9_out, or_10_out, or_11_out);
  and and_4 (out_3[0], or_12_out, or_13_out);

  assign out_2 = in_1;
  assign out_4 = out_3;
endmodule
