// Logisim project ods3.circ as structural Verilog: 1 circuit, main circuit main
module main (
  input  [7:0] in_1,
  input  A,
  input  [7:0] in_3,
  input  B,
  input  C,
  output [7:0] out_6,
  output [7:0] out_7,
  output [7:0] out_8,
  output [7:0] out_9
);

  wire and_1_out, and_2_out, and_3_out, and_4_out, and_5_out, and_6_out, and_7_out, and_8_out, and_9_out,
       and_10_out, and_11_out, and_12_out, and_13_out, and_14_out, and_16_out, and_17_out, and_18_out,
       and_20_out, and_21_out, and_22_out, and_24_out, and_25_out, and_26_out, and_28_out, and_29_out,
       and_30_out, and_32_out, and_33_out, and_34_out, and_36_out, and_37_out, and_38_out, and_40_out,
       and_41_out, and_42_out, and_44_out, and_45_out, not_1_out, not_2_out, not_3_out, not_4_out, not_5_out,
       not_6_out, not_7_out, not_8_out, not_9_out, not_10_out, not_11_out, not_12_out, not_13_out,
       not_14_out, not_15_out, not_16_out, not_17_out, not_18_out, not_19_out, not_20_out, not_21_out,
       not_22_out, not_23_out, not_24_out, not_25_out, not_26_out, not_27_out, or_1_out, or_2_out, or_3_out,
       or_4_out, or_5_out, or_6_out, or_7_out, or_8_out, or_9_out, or_10_out, or_11_out, or_12_out,
       or_13_out, or_14_out, or_15_out, or_16_out, or_17_out, or_18_out, or_19_out, or_20_out, or_21_out,
       or_22_out, or_23_out, or_24_out, or_25_out, or_26_out, or_27_out, or_28_out, or_29_out, or_30_out,
       or_31_out, or_32_out, or_33_out, or_34_out, or_35_out, or_36_out, or_37_out, or_38_out, or_39_out,
       or_40_out, or_41_out, or_42_out, or_43_out, or_44_out, or_45_out, or_46_out, or_47_out, or_48_out,
       or_49_out, or_50_out, or_51_out, or_52_out, or_53_out, or_54_out, or_55_out, or_56_out, or_57_out,
       or_58_out, or_59_out, or_60_out, or_61_out, or_62_out, or_63_out, or_64_out, or_65_out, or_66_out,
       or_67_out, or_68_out, or_69_out, or_70_out, or_71_out, or_72_out, or_73_out, or_74_out, or_75_out,
       or_76_out, or_77_out, or_78_out, or_79_out, or_80_out, or_81_out, or_82_out, or_83_out, or_84_out,
       or_85_out, or_86_out, or_87_out, or_88_out, or_89_out, or_90_out, or_91_out, or_92_out, or_93_out,
       or_94_out, or_95_out, or_96_out, or_97_out, or_98_out, or_99_out;

  not not_1 (not_1_out, A);
  not not_2 (not_2_out, B);
  not not_3 (not_3_out, C);
  or or_1 (or_1_out, A, B);
  or or_2 (or_2_out, A, not_2_out);
  or or_3 (or_3_out, not_1_out, B);
  or or_4 (or_4_out, not_1_out, not_2_out);
  or or_5 (or_5_out, A, B);
  or or_6 (or_6_out, A, C);
  or or_7 (or_7_out, B, C);
  or or_8 (or_8_out, or_1_out, C);
  or or_9 (or_9_out, or_2_out, not_3_out);
  or or_10 (or_10_out, or_3_out, not_3_out);
  or or_11 (or_11_out, or_4_out, C);
  and and_1 (and_1_out, or_5_out, or_6_out);
  and and_2 (and_2_out, or_8_out, or_9_out);
  and and_3 (and_3_out, or_10_out, or_11_out);
  and and_4 (and_4_out, and_1_out, or_7_out);
  LED led_1 (.in(and_5_out));
  and and_5 (and_5_out, and_2_out, and_3_out);
  LED led_2 (.in(and_4_out));
  not not_4 (not_4_out, in_3[0]);
  not not_5 (not_5_out, in_1[0]);
  not not_6 (not_6_out, 1'b0);
  not not_7 (not_7_out, in_3[1]);
  not not_8 (not_8_out, in_1[1]);
  not not_9 (not_9_out, and_17_out);
  not not_10 (not_10_out, in_3[2]);
  not not_11 (not_11_out, in_1[2]);
  not not_12 (not_12_out, and_21_out);
  not not_13 (not_13_out, in_3[3]);
  not not_14 (not_14_out, in_1[3]);
  not not_15 (not_15_out, and_25_out);
  not not_16 (not_16_out, in_3[4]);
  not not_17 (not_17_out, in_1[4]);
  not not_18 (not_18_out, and_29_out);
  not not_19 (not_19_out, in_3[5]);
  not not_20 (not_20_out, in_1[5]);
  not not_21 (not_21_out, and_33_out);
  not not_22 (not_22_out, in_3[6]);
  not not_23 (not_23_out, in_1[6]);
  not not_24 (not_24_out, and_37_out);
  not not_25 (not_25_out, in_3[7]);
  not not_26 (not_26_out, in_1[7]);
  not not_27 (not_27_out, and_41_out);
  or or_12 (or_12_out, in_3[0], in_1[0]);
  or or_13 (or_13_out, or_12_out, 1'b0);
  or or_14 (or_14_out, in_3[0], not_5_out);
  or or_15 (or_15_out, or_14_out, not_6_out);
  or or_16 (or_16_out, not_4_out, in_1[0]);
  or or_17 (or_17_out, or_16_out, not_6_out);
  or or_18 (or_18_out, not_4_out, not_5_out);
  or or_19 (or_19_out, or_18_out, 1'b0);
  or or_20 (or_20_out, in_3[0], in_1[0]);
  or or_21 (or_21_out, in_3[0], 1'b0);
  or or_22 (or_22_out, in_1[0], 1'b0);
  or or_23 (or_23_out, in_3[1], in_1[1]);
  or or_24 (or_24_out, or_23_out, and_17_out);
  or or_25 (or_25_out, in_3[1], not_8_out);
  or or_26 (or_26_out, or_25_out, not_9_out);
  or or_27 (or_27_out, not_7_out, in_1[1]);
  or or_28 (or_28_out, or_27_out, not_9_out);
  or or_29 (or_29_out, not_7_out, not_8_out);
  or or_30 (or_30_out, or_29_out, and_17_out);
  or or_31 (or_31_out, in_3[1], in_1[1]);
  or or_32 (or_32_out, in_3[1], and_17_out);
  or or_33 (or_33_out, in_1[1], and_17_out);
  or or_34 (or_34_out, in_3[2], in_1[2]);
  or or_35 (or_35_out, or_34_out, and_21_out);
  or or_36 (or_36_out, in_3[2], not_11_out);
  or or_37 (or_37_out, or_36_out, not_12_out);
  or or_38 (or_38_out, not_10_out, in_1[2]);
  or or_39 (or_39_out, or_38_out, not_12_out);
  or or_40 (or_40_out, not_10_out, not_11_out);
  or or_41 (or_41_out, or_40_out, and_21_out);
  or or_42 (or_42_out, in_3[2], in_1[2]);
  or or_43 (or_43_out, in_3[2], and_21_out);
  or or_44 (or_44_out, in_1[2], and_21_out);
  or or_45 (or_45_out, in_3[3], in_1[3]);
  or or_46 (or_46_out, or_45_out, and_25_out);
  or or_47 (or_47_out, in_3[3], not_14_out);
  or or_48 (or_48_out, or_47_out, not_15_out);
  or or_49 (or_49_out, not_13_out, in_1[3]);
  or or_50 (or_50_out, or_49_out, not_15_out);
  or or_51 (or_51_out, not_13_out, not_14_out);
  or or_52 (or_52_out, or_51_out, and_25_out);
  or or_53 (or_53_out, in_3[3], in_1[3]);
  or or_54 (or_54_out, in_3[3], and_25_out);
  or or_55 (or_55_out, in_1[3], and_25_out);
  or or_56 (or_56_out, in_3[4], in_1[4]);
  or or_57 (or_57_out, or_56_out, and_29_out);
  or or_58 (or_58_out, in_3[4], not_17_out);
  or or_59 (or_59_out, or_58_out, not_18_out);
  or or_60 (or_60_out, not_16_out, in_1[4]);
  or or_61 (or_61_out, or_60_out, not_18_out);
  or or_62 (or_62_out, not_16_out, not_17_out);
  or or_63 (or_63_out, or_62_out, and_29_out);
  or or_64 (or_64_out, in_3[4], in_1[4]);
  or or_65 (or_65_out, in_3[4], and_29_out);
  or or_66 (or_66_out, in_1[4], and_29_out);
  or or_67 (or_67_out, in_3[5], in_1[5]);
  or or_68 (or_68_out, or_67_out, and_33_out);
  or or_69 (or_69_out, in_3[5], not_20_out);
  or or_70 (or_70_out, or_69_out, not_21_out);
  or or_71 (or_71_out, not_19_out, in_1[5]);
  or or_72 (or_72_out, or_71_out, not_21_out);
  or or_73 (or_73_out, not_19_out, not_20_out);
  or or_74 (or_74_out, or_73_out, and_33_out);
  or or_75 (or_75_out, in_3[5], in_1[5]);
  or or_76 (or_76_out, in_3[5], and_33_out);
  or or_77 (or_77_out, in_1[5], and_33_out);
  or or_78 (or_78_out, in_3[6], in_1[6]);
  or or_79 (or_79_out, or_78_out, and_37_out);
  or or_80 (or_80_out, in_3[6], not_23_out);
  or or_81 (or_81_out, or_80_out, not_24_out);
  or or_82 (or_82_out, not_22_out, in_1[6]);
  or or_83 (or_83_out, or_82_out, not_24_out);
  or or_84 (or_84_out, not_22_out, not_23_out);
  or or_85 (or_85_out, or_84_out, and_37_out);
  or or_86 (or_86_out, in_3[6], in_1[6]);
  or or_87 (or_87_out, in_3[6], and_37_out);
  or or_88 (or_88_out, in_1[6], and_37_out);
  or or_89 (or_89_out, in_3[7], in_1[7]);
  or or_90 (or_90_out, or_89_out, and_41_out);
  or or_91 (or_91_out, in_3[7], not_26_out);
  or or_92 (or_92_out, or_91_out, not_27_out);
  or or_93 (or_93_out, not_25_out, in_1[7]);
  or or_94 (or_94_out, or_93_out, not_27_out);
  or or_95 (or_95_out, not_25_out, not_26_out);
  or or_96 (or_96_out, or_95_out, and_41_out);
  or or_97 (or_97_out, in_3[7], in_1[7]);
  or or_98 (or_98_out, in_3[7], and_41_out);
  or or_99 (or_99_out, in_1[7], and_41_out);
  and and_6 (and_6_out, or_20_out, or_21_out);
  and and_7 (and_7_out, or_31_out, or_32_out);
  and and_8 (and_8_out, or_42_out, or_43_out);
  and and_9 (and_9_out, or_53_out, or_54_out);
  and and_10 (and_10_out, or_64_out, or_65_out);
  and and_11 (and_11_out, or_75_out, or_76_out);
  and and_12 (and_12_out, or_86_out, or_87_out);
  and and_13 (and_13_out, or_97_out, or_98_out);
  and and_14 (and_14_out, or_13_out, or_15_out);
  and and_15 (out_8[0], and_14_out, and_16_out);
  and and_16 (and_16_out, or_17_out, or_19_out);
  and and_17 (and_17_out, and_6_out, or_22_out);
  and and_18 (and_18_out, or_24_out, or_26_out);
  and and_19 (out_8[1], and_18_out, and_20_out);
  and and_20 (and_20_out, or_28_out, or_30_out);
  and and_21 (and_21_out, and_7_out, or_33_out);
  and and_22 (and_22_out, or_35_out, or_37_out);
  and and_23 (out_8[2], and_22_out, and_24_out);
  and and_24 (and_24_out, or_39_out, or_41_out);
  and and_25 (and_25_out, and_8_out, or_44_out);
  and and_26 (and_26_out, or_46_out, or_48_out);
  and and_27 (out_8[3], and_26_out, and_28_out);
  and and_28 (and_28_out, or_50_out, or_52_out);
  and and_29 (and_29_out, and_9_out, or_55_out);
  and and_30 (and_30_out, or_57_out, or_59_out);
  and and_31 (out_8[4], and_30_out, and_32_out);
  and and_32 (and_32_out, or_61_out, or_63_out);
  and and_33 (and_33_out, and_10_out, or_66_out);
  and and_34 (and_34_out, or_68_out, or_70_out);
  and and_35 (out_8[5], and_34_out, and_36_out);
  and and_36 (and_36_out, or_72_out, or_74_out);
  and and_37 (and_37_out, and_11_out, or_77_out);
  and and_38 (and_38_out, or_79_out, or_81_out);
  and and_39 (out_8[6], and_38_out, and_40_out);
  and and_40 (and_40_out, or_83_out, or_85_out);
  and and_41 (and_41_out, and_12_out, or_88_out);
  and and_42 (and_42_out, or_90_out, or_92_out);
  and and_43 (out_8[7], and_42_out, and_44_out);
  and and_44 (and_44_out, or_94_out, or_96_out);
  and and_45 (and_45_out, and_13_out, or_99_out);
  LED led_3 (.in(and_45_out));

  assign out_6 = in_1;
  assign out_7 = in_3;
  assign out_9 = out_8;

  // Notes on the sheet:
  //   x1
  //   x2
  //   x3
  //   !x1
  //   !x2
  //   !x3
  //   x3
  //   x1
  //   x2
  //   x3
  //   x2
  //   x1
  //   !x2
  //   !x1
  //   !x3
  //   !x2
  //   !x1
  //   !x3
endmodule
